// Logisim project Group.circ as structural Verilog: 7 circuits, main circuit 1 bit Alu
// 1 Bit ALU
module _1_bit_Alu (
  input  B,
  input  A,
  input  Carry_In,
  input  [1:0] Operation,
  output Result,
  output Carry_Out
);

  wire adder_1_out, and_1_out, bitselector_1_out, multiplexer_1_out, not_1_out, not_2_out, or_1_out;

  Multiplexer #(.enable("false")) multiplexer_1 (
    .in0(B), .in1(not_1_out), .out(multiplexer_1_out), .sel(bitselector_1_out));
  not not_1 (not_1_out, B);
  BitSelector #(.width(2)) bitselector_1 (.in(Operation), .out(bitselector_1_out), .sel(1'b1));
  not not_2 (not_2_out, multiplexer_1_out);
  and and_1 (and_1_out, A, not_2_out);
  or or_1 (or_1_out, A, multiplexer_1_out);
  Adder #(.width(1)) adder_1 (.a(A), .b(multiplexer_1_out), .out(adder_1_out), .cin(Carry_In), .cout(Carry_Out));
  Multiplexer #(.select(2), .enable("false")) multiplexer_2 (
    .in0(or_1_out), .in1(adder_1_out), .in2(and_1_out), .in3(adder_1_out), .out(Result), .sel(Operation));
endmodule

// 16 Bit Alu
module _16_bit_ALu (
  input  Carry_In,
  input  [15:0] A,
  input  [15:0] B,
  input  [1:0] Operation,
  output [15:0] Result,
  output ZERO,
  output Over_Flow,
  output Carry_Out
);

  wire n1_bit_alu_1_carry_out, n1_bit_alu_2_carry_out, n1_bit_alu_3_carry_out, n1_bit_alu_4_carry_out,
       n1_bit_alu_5_carry_out, n1_bit_alu_6_carry_out, n1_bit_alu_7_carry_out, n1_bit_alu_8_carry_out,
       n1_bit_alu_9_carry_out, n1_bit_alu_10_carry_out, n1_bit_alu_11_carry_out, n1_bit_alu_12_carry_out,
       n1_bit_alu_13_carry_out, n1_bit_alu_14_carry_out, n1_bit_alu_15_carry_out;

  _1_bit_Alu u_1_bit_alu_1 (
    .A(A[0]), .B(B[0]), .Carry_In(Carry_In), .Result(Result[0]), .Operation(Operation),
    .Carry_Out(n1_bit_alu_1_carry_out));
  _1_bit_Alu u_1_bit_alu_2 (
    .A(A[1]), .B(B[1]), .Carry_In(n1_bit_alu_1_carry_out), .Result(Result[1]), .Operation(Operation),
    .Carry_Out(n1_bit_alu_2_carry_out));
  _1_bit_Alu u_1_bit_alu_3 (
    .A(A[2]), .B(B[2]), .Carry_In(n1_bit_alu_2_carry_out), .Result(Result[2]), .Operation(Operation),
    .Carry_Out(n1_bit_alu_3_carry_out));
  _1_bit_Alu u_1_bit_alu_4 (
    .A(A[3]), .B(B[3]), .Carry_In(n1_bit_alu_3_carry_out), .Result(Result[3]), .Operation(Operation),
    .Carry_Out(n1_bit_alu_4_carry_out));
  _1_bit_Alu u_1_bit_alu_5 (
    .A(A[4]), .B(B[4]), .Carry_In(n1_bit_alu_4_carry_out), .Result(Result[4]), .Operation(Operation),
    .Carry_Out(n1_bit_alu_5_carry_out));
  _1_bit_Alu u_1_bit_alu_6 (
    .A(A[5]), .B(B[5]), .Carry_In(n1_bit_alu_5_carry_out), .Result(Result[5]), .Operation(Operation),
    .Carry_Out(n1_bit_alu_6_carry_out));
  _1_bit_Alu u_1_bit_alu_7 (
    .A(A[6]), .B(B[6]), .Carry_In(n1_bit_alu_6_carry_out), .Result(Result[6]), .Operation(Operation),
    .Carry_Out(n1_bit_alu_7_carry_out));
  _1_bit_Alu u_1_bit_alu_8 (
    .A(A[7]), .B(B[7]), .Carry_In(n1_bit_alu_7_carry_out), .Result(Result[7]), .Operation(Operation),
    .Carry_Out(n1_bit_alu_8_carry_out));
  _1_bit_Alu u_1_bit_alu_9 (
    .A(A[8]), .B(B[8]), .Carry_In(n1_bit_alu_8_carry_out), .Result(Result[8]), .Operation(Operation),
    .Carry_Out(n1_bit_alu_9_carry_out));
  _1_bit_Alu u_1_bit_alu_10 (
    .A(A[9]), .B(B[9]), .Carry_In(n1_bit_alu_9_carry_out), .Result(Result[9]), .Operation(Operation),
    .Carry_Out(n1_bit_alu_10_carry_out));
  _1_bit_Alu u_1_bit_alu_11 (
    .A(A[10]), .B(B[10]), .Carry_In(n1_bit_alu_10_carry_out), .Result(Result[10]), .Operation(Operation),
    .Carry_Out(n1_bit_alu_11_carry_out));
  _1_bit_Alu u_1_bit_alu_12 (
    .A(A[11]), .B(B[11]), .Carry_In(n1_bit_alu_11_carry_out), .Result(Result[11]), .Operation(Operation),
    .Carry_Out(n1_bit_alu_12_carry_out));
  _1_bit_Alu u_1_bit_alu_13 (
    .A(A[12]), .B(B[12]), .Carry_In(n1_bit_alu_12_carry_out), .Result(Result[12]), .Operation(Operation),
    .Carry_Out(n1_bit_alu_13_carry_out));
  _1_bit_Alu u_1_bit_alu_14 (
    .A(A[13]), .B(B[13]), .Carry_In(n1_bit_alu_13_carry_out), .Result(Result[13]), .Operation(Operation),
    .Carry_Out(n1_bit_alu_14_carry_out));
  _1_bit_Alu u_1_bit_alu_15 (
    .A(A[14]), .B(B[14]), .Carry_In(n1_bit_alu_14_carry_out), .Result(Result[14]), .Operation(Operation),
    .Carry_Out(n1_bit_alu_15_carry_out));
  _1_bit_Alu u_1_bit_alu_16 (
    .A(A[15]), .B(B[15]), .Carry_In(n1_bit_alu_15_carry_out), .Result(Result[15]), .Operation(Operation),
    .Carry_Out(Carry_Out));
  xor xor_1 (Over_Flow, n1_bit_alu_15_carry_out, Carry_Out);
  nor nor_1 (ZERO, Result[0], Result[1], Result[2], Result[3], Result[4], Result[5], Result[6], Result[7], Result[8], Result[9], Result[10], Result[11], Result[12], Result[13], Result[14], Result[15]);
endmodule

module Expermient (
  input  [15:0] A,
  input  [15:0] B,
  input  [1:0] Input_Operation_Control,
  input  Circuit_Control,
  output ZERO,
  output OverFlow,
  output [15:0] Result,
  output CarryOut,
  output [31:0] Result_2
);

  wire bitselector_1_out, bitselector_2_out, Carry_In_out, multiplexer_1_out, not_1_out, not_2_out;
  wire [15:0] bit_extender_2_out, n16_bit_alu_1_result;
  wire [31:0] _16_bit_Multiplier_result, bit_extender_1_out;

  BitSelector #(.width(2)) bitselector_1 (.in(Input_Operation_Control), .out(bitselector_1_out), .sel(1'b0));
  BitSelector #(.width(2)) bitselector_2 (.in(Input_Operation_Control), .out(bitselector_2_out), .sel(1'b1));
  and Carry_In (Carry_In_out, bitselector_1_out, bitselector_2_out);
  _16_bit_ALu u_16_bit_alu_1 (
    .A(A), .B(B), .Carry_In(Carry_In_out), .Result(n16_bit_alu_1_result), .Over_Flow(OverFlow),
    .Carry_Out(CarryOut), .ZERO(ZERO), .Operation(Input_Operation_Control));
  _16_bit_Multiplier _16_bit_Multiplier (.A(A), .B(B), .Result(_16_bit_Multiplier_result));
  Multiplexer #(.enable("false")) multiplexer_1 (
    .in0(1'b1), .in1(not_1_out), .out(multiplexer_1_out), .sel(Circuit_Control));
  not not_1 (not_1_out, 1'b1);
  not not_2 (not_2_out, multiplexer_1_out);
  assign bit_extender_1_out = {{31{not_2_out}}, not_2_out};  // Bit_Extender bit_extender_1
  assign bit_extender_2_out = {{15{multiplexer_1_out}}, multiplexer_1_out};  // Bit_Extender bit_extender_2
  assign Result_2 = bit_extender_1_out & _16_bit_Multiplier_result;  // AND_Gate and_1, 32 bits wide
  assign Result = n16_bit_alu_1_result & bit_extender_2_out;  // AND_Gate and_2, 16 bits wide
endmodule

module _16_bit_Multiplier (
  input  [15:0] A,
  input  [15:0] B,
  output [31:0] Result
);

  wire [14:0] _16_AND_Gates_13_c1;
  wire [15:0] _16_AND_Gates_2_c0, _16_AND_Gates_3_c0, _16_AND_Gates_4_c0, _16_AND_Gates_5_c0,
       _16_AND_Gates_6_c0, _16_AND_Gates_7_c0, _16_AND_Gates_8_c0, _16_AND_Gates_9_c0, _16_AND_Gates_10_c0,
       _16_AND_Gates_11_c0, _16_AND_Gates_12_c0, _16_AND_Gates_14_c0, _16_AND_Gates_15_c0,
       _16_AND_Gates_16_c0, _16_AND_Gates_c0, _16_Bit_parallel_adder_2_c1, _16_Bit_parallel_adder_3_c1,
       _16_Bit_parallel_adder_4_c1, _16_Bit_parallel_adder_5_c1, _16_Bit_parallel_adder_6_c1,
       _16_Bit_parallel_adder_7_c1, _16_Bit_parallel_adder_8_c1, _16_Bit_parallel_adder_9_c1,
       _16_Bit_parallel_adder_10_c1, _16_Bit_parallel_adder_11_c1, _16_Bit_parallel_adder_12_c1,
       _16_Bit_parallel_adder_13_c1, _16_Bit_parallel_adder_14_c1, _16_Bit_parallel_adder_c1;

  _16_And_Gates _16_AND_Gates (
    .B(B), .in_2(A[2]), .C15(_16_AND_Gates_c0[15]), .C14(_16_AND_Gates_c0[14]), .C13(_16_AND_Gates_c0[13]),
    .C12(_16_AND_Gates_c0[12]), .C11(_16_AND_Gates_c0[11]), .C10(_16_AND_Gates_c0[10]),
    .C9(_16_AND_Gates_c0[9]), .C8(_16_AND_Gates_c0[8]), .C7(_16_AND_Gates_c0[7]), .C6(_16_AND_Gates_c0[6]),
    .C5(_16_AND_Gates_c0[5]), .C4(_16_AND_Gates_c0[4]), .C3(_16_AND_Gates_c0[3]), .C2(_16_AND_Gates_c0[2]),
    .C1(_16_AND_Gates_c0[1]), .C0(_16_AND_Gates_c0[0]));
  _16_And_Gates _16_AND_Gates_2 (
    .B(B), .in_2(A[3]), .C15(_16_AND_Gates_2_c0[15]), .C14(_16_AND_Gates_2_c0[14]),
    .C13(_16_AND_Gates_2_c0[13]), .C12(_16_AND_Gates_2_c0[12]), .C11(_16_AND_Gates_2_c0[11]),
    .C10(_16_AND_Gates_2_c0[10]), .C9(_16_AND_Gates_2_c0[9]), .C8(_16_AND_Gates_2_c0[8]),
    .C7(_16_AND_Gates_2_c0[7]), .C6(_16_AND_Gates_2_c0[6]), .C5(_16_AND_Gates_2_c0[5]),
    .C4(_16_AND_Gates_2_c0[4]), .C3(_16_AND_Gates_2_c0[3]), .C2(_16_AND_Gates_2_c0[2]),
    .C1(_16_AND_Gates_2_c0[1]), .C0(_16_AND_Gates_2_c0[0]));
  _16_And_Gates _16_AND_Gates_3 (
    .B(B), .in_2(A[4]), .C15(_16_AND_Gates_3_c0[15]), .C14(_16_AND_Gates_3_c0[14]),
    .C13(_16_AND_Gates_3_c0[13]), .C12(_16_AND_Gates_3_c0[12]), .C11(_16_AND_Gates_3_c0[11]),
    .C10(_16_AND_Gates_3_c0[10]), .C9(_16_AND_Gates_3_c0[9]), .C8(_16_AND_Gates_3_c0[8]),
    .C7(_16_AND_Gates_3_c0[7]), .C6(_16_AND_Gates_3_c0[6]), .C5(_16_AND_Gates_3_c0[5]),
    .C4(_16_AND_Gates_3_c0[4]), .C3(_16_AND_Gates_3_c0[3]), .C2(_16_AND_Gates_3_c0[2]),
    .C1(_16_AND_Gates_3_c0[1]), .C0(_16_AND_Gates_3_c0[0]));
  _16_And_Gates _16_AND_Gates_4 (
    .B(B), .in_2(A[1]), .C15(_16_AND_Gates_4_c0[15]), .C14(_16_AND_Gates_4_c0[14]),
    .C13(_16_AND_Gates_4_c0[13]), .C12(_16_AND_Gates_4_c0[12]), .C11(_16_AND_Gates_4_c0[11]),
    .C10(_16_AND_Gates_4_c0[10]), .C9(_16_AND_Gates_4_c0[9]), .C8(_16_AND_Gates_4_c0[8]),
    .C7(_16_AND_Gates_4_c0[7]), .C6(_16_AND_Gates_4_c0[6]), .C5(_16_AND_Gates_4_c0[5]),
    .C4(_16_AND_Gates_4_c0[4]), .C3(_16_AND_Gates_4_c0[3]), .C2(_16_AND_Gates_4_c0[2]),
    .C1(_16_AND_Gates_4_c0[1]), .C0(_16_AND_Gates_4_c0[0]));
  _16_And_Gates _16_AND_Gates_5 (
    .B(B), .in_2(A[5]), .C15(_16_AND_Gates_5_c0[15]), .C14(_16_AND_Gates_5_c0[14]),
    .C13(_16_AND_Gates_5_c0[13]), .C12(_16_AND_Gates_5_c0[12]), .C11(_16_AND_Gates_5_c0[11]),
    .C10(_16_AND_Gates_5_c0[10]), .C9(_16_AND_Gates_5_c0[9]), .C8(_16_AND_Gates_5_c0[8]),
    .C7(_16_AND_Gates_5_c0[7]), .C6(_16_AND_Gates_5_c0[6]), .C5(_16_AND_Gates_5_c0[5]),
    .C4(_16_AND_Gates_5_c0[4]), .C3(_16_AND_Gates_5_c0[3]), .C2(_16_AND_Gates_5_c0[2]),
    .C1(_16_AND_Gates_5_c0[1]), .C0(_16_AND_Gates_5_c0[0]));
  _16_And_Gates _16_AND_Gates_6 (
    .B(B), .in_2(A[6]), .C15(_16_AND_Gates_6_c0[15]), .C14(_16_AND_Gates_6_c0[14]),
    .C13(_16_AND_Gates_6_c0[13]), .C12(_16_AND_Gates_6_c0[12]), .C11(_16_AND_Gates_6_c0[11]),
    .C10(_16_AND_Gates_6_c0[10]), .C9(_16_AND_Gates_6_c0[9]), .C8(_16_AND_Gates_6_c0[8]),
    .C7(_16_AND_Gates_6_c0[7]), .C6(_16_AND_Gates_6_c0[6]), .C5(_16_AND_Gates_6_c0[5]),
    .C4(_16_AND_Gates_6_c0[4]), .C3(_16_AND_Gates_6_c0[3]), .C2(_16_AND_Gates_6_c0[2]),
    .C1(_16_AND_Gates_6_c0[1]), .C0(_16_AND_Gates_6_c0[0]));
  _16_And_Gates _16_AND_Gates_7 (
    .B(B), .in_2(A[7]), .C15(_16_AND_Gates_7_c0[15]), .C14(_16_AND_Gates_7_c0[14]),
    .C13(_16_AND_Gates_7_c0[13]), .C12(_16_AND_Gates_7_c0[12]), .C11(_16_AND_Gates_7_c0[11]),
    .C10(_16_AND_Gates_7_c0[10]), .C9(_16_AND_Gates_7_c0[9]), .C8(_16_AND_Gates_7_c0[8]),
    .C7(_16_AND_Gates_7_c0[7]), .C6(_16_AND_Gates_7_c0[6]), .C5(_16_AND_Gates_7_c0[5]),
    .C4(_16_AND_Gates_7_c0[4]), .C3(_16_AND_Gates_7_c0[3]), .C2(_16_AND_Gates_7_c0[2]),
    .C1(_16_AND_Gates_7_c0[1]), .C0(_16_AND_Gates_7_c0[0]));
  _16_And_Gates _16_AND_Gates_8 (
    .B(B), .in_2(A[8]), .C15(_16_AND_Gates_8_c0[15]), .C14(_16_AND_Gates_8_c0[14]),
    .C13(_16_AND_Gates_8_c0[13]), .C12(_16_AND_Gates_8_c0[12]), .C11(_16_AND_Gates_8_c0[11]),
    .C10(_16_AND_Gates_8_c0[10]), .C9(_16_AND_Gates_8_c0[9]), .C8(_16_AND_Gates_8_c0[8]),
    .C7(_16_AND_Gates_8_c0[7]), .C6(_16_AND_Gates_8_c0[6]), .C5(_16_AND_Gates_8_c0[5]),
    .C4(_16_AND_Gates_8_c0[4]), .C3(_16_AND_Gates_8_c0[3]), .C2(_16_AND_Gates_8_c0[2]),
    .C1(_16_AND_Gates_8_c0[1]), .C0(_16_AND_Gates_8_c0[0]));
  _16_And_Gates _16_AND_Gates_9 (
    .B(B), .in_2(A[9]), .C15(_16_AND_Gates_9_c0[15]), .C14(_16_AND_Gates_9_c0[14]),
    .C13(_16_AND_Gates_9_c0[13]), .C12(_16_AND_Gates_9_c0[12]), .C11(_16_AND_Gates_9_c0[11]),
    .C10(_16_AND_Gates_9_c0[10]), .C9(_16_AND_Gates_9_c0[9]), .C8(_16_AND_Gates_9_c0[8]),
    .C7(_16_AND_Gates_9_c0[7]), .C6(_16_AND_Gates_9_c0[6]), .C5(_16_AND_Gates_9_c0[5]),
    .C4(_16_AND_Gates_9_c0[4]), .C3(_16_AND_Gates_9_c0[3]), .C2(_16_AND_Gates_9_c0[2]),
    .C1(_16_AND_Gates_9_c0[1]), .C0(_16_AND_Gates_9_c0[0]));
  _16_And_Gates _16_AND_Gates_10 (
    .B(B), .in_2(A[10]), .C15(_16_AND_Gates_10_c0[15]), .C14(_16_AND_Gates_10_c0[14]),
    .C13(_16_AND_Gates_10_c0[13]), .C12(_16_AND_Gates_10_c0[12]), .C11(_16_AND_Gates_10_c0[11]),
    .C10(_16_AND_Gates_10_c0[10]), .C9(_16_AND_Gates_10_c0[9]), .C8(_16_AND_Gates_10_c0[8]),
    .C7(_16_AND_Gates_10_c0[7]), .C6(_16_AND_Gates_10_c0[6]), .C5(_16_AND_Gates_10_c0[5]),
    .C4(_16_AND_Gates_10_c0[4]), .C3(_16_AND_Gates_10_c0[3]), .C2(_16_AND_Gates_10_c0[2]),
    .C1(_16_AND_Gates_10_c0[1]), .C0(_16_AND_Gates_10_c0[0]));
  _16_And_Gates _16_AND_Gates_11 (
    .B(B), .in_2(A[11]), .C15(_16_AND_Gates_11_c0[15]), .C14(_16_AND_Gates_11_c0[14]),
    .C13(_16_AND_Gates_11_c0[13]), .C12(_16_AND_Gates_11_c0[12]), .C11(_16_AND_Gates_11_c0[11]),
    .C10(_16_AND_Gates_11_c0[10]), .C9(_16_AND_Gates_11_c0[9]), .C8(_16_AND_Gates_11_c0[8]),
    .C7(_16_AND_Gates_11_c0[7]), .C6(_16_AND_Gates_11_c0[6]), .C5(_16_AND_Gates_11_c0[5]),
    .C4(_16_AND_Gates_11_c0[4]), .C3(_16_AND_Gates_11_c0[3]), .C2(_16_AND_Gates_11_c0[2]),
    .C1(_16_AND_Gates_11_c0[1]), .C0(_16_AND_Gates_11_c0[0]));
  _16_And_Gates _16_AND_Gates_12 (
    .B(B), .in_2(A[12]), .C15(_16_AND_Gates_12_c0[15]), .C14(_16_AND_Gates_12_c0[14]),
    .C13(_16_AND_Gates_12_c0[13]), .C12(_16_AND_Gates_12_c0[12]), .C11(_16_AND_Gates_12_c0[11]),
    .C10(_16_AND_Gates_12_c0[10]), .C9(_16_AND_Gates_12_c0[9]), .C8(_16_AND_Gates_12_c0[8]),
    .C7(_16_AND_Gates_12_c0[7]), .C6(_16_AND_Gates_12_c0[6]), .C5(_16_AND_Gates_12_c0[5]),
    .C4(_16_AND_Gates_12_c0[4]), .C3(_16_AND_Gates_12_c0[3]), .C2(_16_AND_Gates_12_c0[2]),
    .C1(_16_AND_Gates_12_c0[1]), .C0(_16_AND_Gates_12_c0[0]));
  _16_And_Gates _16_AND_Gates_13 (
    .B(B), .in_2(A[0]), .C15(_16_AND_Gates_13_c1[14]), .C14(_16_AND_Gates_13_c1[13]),
    .C13(_16_AND_Gates_13_c1[12]), .C12(_16_AND_Gates_13_c1[11]), .C11(_16_AND_Gates_13_c1[10]),
    .C10(_16_AND_Gates_13_c1[9]), .C9(_16_AND_Gates_13_c1[8]), .C8(_16_AND_Gates_13_c1[7]),
    .C7(_16_AND_Gates_13_c1[6]), .C6(_16_AND_Gates_13_c1[5]), .C5(_16_AND_Gates_13_c1[4]),
    .C4(_16_AND_Gates_13_c1[3]), .C3(_16_AND_Gates_13_c1[2]), .C2(_16_AND_Gates_13_c1[1]),
    .C1(_16_AND_Gates_13_c1[0]), .C0(Result[0]));
  _16_Bit_parallel_adder _16_Bit_parallel_adder (
    .A(_16_Bit_parallel_adder_4_c1), .B(_16_AND_Gates_c0), .Carry_Out(_16_Bit_parallel_adder_c1[15]),
    .C0(Result[2]), .C1(_16_Bit_parallel_adder_c1[0]), .C2(_16_Bit_parallel_adder_c1[1]),
    .C3(_16_Bit_parallel_adder_c1[2]), .C4(_16_Bit_parallel_adder_c1[3]), .C5(_16_Bit_parallel_adder_c1[4]),
    .C6(_16_Bit_parallel_adder_c1[5]), .C7(_16_Bit_parallel_adder_c1[6]), .C9(_16_Bit_parallel_adder_c1[7]),
    .C8(_16_Bit_parallel_adder_c1[8]), .C10(_16_Bit_parallel_adder_c1[9]),
    .C11(_16_Bit_parallel_adder_c1[10]), .C12(_16_Bit_parallel_adder_c1[11]),
    .C14(_16_Bit_parallel_adder_c1[13]), .C15(_16_Bit_parallel_adder_c1[14]),
    .C13(_16_Bit_parallel_adder_c1[12]));
  _16_Bit_parallel_adder _16_Bit_parallel_adder_2 (
    .A(_16_Bit_parallel_adder_c1), .B(_16_AND_Gates_2_c0), .Carry_Out(_16_Bit_parallel_adder_2_c1[15]),
    .C0(Result[3]), .C1(_16_Bit_parallel_adder_2_c1[0]), .C2(_16_Bit_parallel_adder_2_c1[1]),
    .C3(_16_Bit_parallel_adder_2_c1[2]), .C4(_16_Bit_parallel_adder_2_c1[3]),
    .C5(_16_Bit_parallel_adder_2_c1[4]), .C6(_16_Bit_parallel_adder_2_c1[5]),
    .C7(_16_Bit_parallel_adder_2_c1[6]), .C9(_16_Bit_parallel_adder_2_c1[7]),
    .C8(_16_Bit_parallel_adder_2_c1[8]), .C10(_16_Bit_parallel_adder_2_c1[9]),
    .C11(_16_Bit_parallel_adder_2_c1[10]), .C12(_16_Bit_parallel_adder_2_c1[11]),
    .C14(_16_Bit_parallel_adder_2_c1[13]), .C15(_16_Bit_parallel_adder_2_c1[14]),
    .C13(_16_Bit_parallel_adder_2_c1[12]));
  _16_Bit_parallel_adder _16_Bit_parallel_adder_3 (
    .A(_16_Bit_parallel_adder_2_c1), .B(_16_AND_Gates_3_c0), .Carry_Out(_16_Bit_parallel_adder_3_c1[15]),
    .C0(Result[4]), .C1(_16_Bit_parallel_adder_3_c1[0]), .C2(_16_Bit_parallel_adder_3_c1[1]),
    .C3(_16_Bit_parallel_adder_3_c1[2]), .C4(_16_Bit_parallel_adder_3_c1[3]),
    .C5(_16_Bit_parallel_adder_3_c1[4]), .C6(_16_Bit_parallel_adder_3_c1[5]),
    .C7(_16_Bit_parallel_adder_3_c1[6]), .C9(_16_Bit_parallel_adder_3_c1[7]),
    .C8(_16_Bit_parallel_adder_3_c1[8]), .C10(_16_Bit_parallel_adder_3_c1[9]),
    .C11(_16_Bit_parallel_adder_3_c1[10]), .C12(_16_Bit_parallel_adder_3_c1[11]),
    .C14(_16_Bit_parallel_adder_3_c1[13]), .C15(_16_Bit_parallel_adder_3_c1[14]),
    .C13(_16_Bit_parallel_adder_3_c1[12]));
  _16_And_Gates _16_AND_Gates_14 (
    .B(B), .in_2(A[13]), .C15(_16_AND_Gates_14_c0[15]), .C14(_16_AND_Gates_14_c0[14]),
    .C13(_16_AND_Gates_14_c0[13]), .C12(_16_AND_Gates_14_c0[12]), .C11(_16_AND_Gates_14_c0[11]),
    .C10(_16_AND_Gates_14_c0[10]), .C9(_16_AND_Gates_14_c0[9]), .C8(_16_AND_Gates_14_c0[8]),
    .C7(_16_AND_Gates_14_c0[7]), .C6(_16_AND_Gates_14_c0[6]), .C5(_16_AND_Gates_14_c0[5]),
    .C4(_16_AND_Gates_14_c0[4]), .C3(_16_AND_Gates_14_c0[3]), .C2(_16_AND_Gates_14_c0[2]),
    .C1(_16_AND_Gates_14_c0[1]), .C0(_16_AND_Gates_14_c0[0]));
  _16_And_Gates _16_AND_Gates_15 (
    .B(B), .in_2(A[14]), .C15(_16_AND_Gates_15_c0[15]), .C14(_16_AND_Gates_15_c0[14]),
    .C13(_16_AND_Gates_15_c0[13]), .C12(_16_AND_Gates_15_c0[12]), .C11(_16_AND_Gates_15_c0[11]),
    .C10(_16_AND_Gates_15_c0[10]), .C9(_16_AND_Gates_15_c0[9]), .C8(_16_AND_Gates_15_c0[8]),
    .C7(_16_AND_Gates_15_c0[7]), .C6(_16_AND_Gates_15_c0[6]), .C5(_16_AND_Gates_15_c0[5]),
    .C4(_16_AND_Gates_15_c0[4]), .C3(_16_AND_Gates_15_c0[3]), .C2(_16_AND_Gates_15_c0[2]),
    .C1(_16_AND_Gates_15_c0[1]), .C0(_16_AND_Gates_15_c0[0]));
  _16_And_Gates _16_AND_Gates_16 (
    .B(B), .in_2(A[15]), .C15(_16_AND_Gates_16_c0[15]), .C14(_16_AND_Gates_16_c0[14]),
    .C13(_16_AND_Gates_16_c0[13]), .C12(_16_AND_Gates_16_c0[12]), .C11(_16_AND_Gates_16_c0[11]),
    .C10(_16_AND_Gates_16_c0[10]), .C9(_16_AND_Gates_16_c0[9]), .C8(_16_AND_Gates_16_c0[8]),
    .C7(_16_AND_Gates_16_c0[7]), .C6(_16_AND_Gates_16_c0[6]), .C5(_16_AND_Gates_16_c0[5]),
    .C4(_16_AND_Gates_16_c0[4]), .C3(_16_AND_Gates_16_c0[3]), .C2(_16_AND_Gates_16_c0[2]),
    .C1(_16_AND_Gates_16_c0[1]), .C0(_16_AND_Gates_16_c0[0]));
  _16_Bit_parallel_adder _16_Bit_parallel_adder_4 (
    .A({1'b0, _16_AND_Gates_13_c1}), .B(_16_AND_Gates_4_c0), .Carry_Out(_16_Bit_parallel_adder_4_c1[15]),
    .C0(Result[1]), .C1(_16_Bit_parallel_adder_4_c1[0]), .C2(_16_Bit_parallel_adder_4_c1[1]),
    .C3(_16_Bit_parallel_adder_4_c1[2]), .C4(_16_Bit_parallel_adder_4_c1[3]),
    .C5(_16_Bit_parallel_adder_4_c1[4]), .C6(_16_Bit_parallel_adder_4_c1[5]),
    .C7(_16_Bit_parallel_adder_4_c1[6]), .C9(_16_Bit_parallel_adder_4_c1[7]),
    .C8(_16_Bit_parallel_adder_4_c1[8]), .C10(_16_Bit_parallel_adder_4_c1[9]),
    .C11(_16_Bit_parallel_adder_4_c1[10]), .C12(_16_Bit_parallel_adder_4_c1[11]),
    .C14(_16_Bit_parallel_adder_4_c1[13]), .C15(_16_Bit_parallel_adder_4_c1[14]),
    .C13(_16_Bit_parallel_adder_4_c1[12]));
  _16_Bit_parallel_adder _16_Bit_parallel_adder_5 (
    .A(_16_Bit_parallel_adder_3_c1), .B(_16_AND_Gates_5_c0), .Carry_Out(_16_Bit_parallel_adder_5_c1[15]),
    .C0(Result[5]), .C1(_16_Bit_parallel_adder_5_c1[0]), .C2(_16_Bit_parallel_adder_5_c1[1]),
    .C3(_16_Bit_parallel_adder_5_c1[2]), .C4(_16_Bit_parallel_adder_5_c1[3]),
    .C5(_16_Bit_parallel_adder_5_c1[4]), .C6(_16_Bit_parallel_adder_5_c1[5]),
    .C7(_16_Bit_parallel_adder_5_c1[6]), .C9(_16_Bit_parallel_adder_5_c1[7]),
    .C8(_16_Bit_parallel_adder_5_c1[8]), .C10(_16_Bit_parallel_adder_5_c1[9]),
    .C11(_16_Bit_parallel_adder_5_c1[10]), .C12(_16_Bit_parallel_adder_5_c1[11]),
    .C14(_16_Bit_parallel_adder_5_c1[13]), .C15(_16_Bit_parallel_adder_5_c1[14]),
    .C13(_16_Bit_parallel_adder_5_c1[12]));
  _16_Bit_parallel_adder _16_Bit_parallel_adder_6 (
    .A(_16_Bit_parallel_adder_5_c1), .B(_16_AND_Gates_6_c0), .Carry_Out(_16_Bit_parallel_adder_6_c1[15]),
    .C0(Result[6]), .C1(_16_Bit_parallel_adder_6_c1[0]), .C2(_16_Bit_parallel_adder_6_c1[1]),
    .C3(_16_Bit_parallel_adder_6_c1[2]), .C4(_16_Bit_parallel_adder_6_c1[3]),
    .C5(_16_Bit_parallel_adder_6_c1[4]), .C6(_16_Bit_parallel_adder_6_c1[5]),
    .C7(_16_Bit_parallel_adder_6_c1[6]), .C9(_16_Bit_parallel_adder_6_c1[7]),
    .C8(_16_Bit_parallel_adder_6_c1[8]), .C10(_16_Bit_parallel_adder_6_c1[9]),
    .C11(_16_Bit_parallel_adder_6_c1[10]), .C12(_16_Bit_parallel_adder_6_c1[11]),
    .C14(_16_Bit_parallel_adder_6_c1[13]), .C15(_16_Bit_parallel_adder_6_c1[14]),
    .C13(_16_Bit_parallel_adder_6_c1[12]));
  _16_Bit_parallel_adder _16_Bit_parallel_adder_7 (
    .A(_16_Bit_parallel_adder_6_c1), .B(_16_AND_Gates_7_c0), .Carry_Out(_16_Bit_parallel_adder_7_c1[15]),
    .C0(Result[7]), .C1(_16_Bit_parallel_adder_7_c1[0]), .C2(_16_Bit_parallel_adder_7_c1[1]),
    .C3(_16_Bit_parallel_adder_7_c1[2]), .C4(_16_Bit_parallel_adder_7_c1[3]),
    .C5(_16_Bit_parallel_adder_7_c1[4]), .C6(_16_Bit_parallel_adder_7_c1[5]),
    .C7(_16_Bit_parallel_adder_7_c1[6]), .C9(_16_Bit_parallel_adder_7_c1[7]),
    .C8(_16_Bit_parallel_adder_7_c1[8]), .C10(_16_Bit_parallel_adder_7_c1[9]),
    .C11(_16_Bit_parallel_adder_7_c1[10]), .C12(_16_Bit_parallel_adder_7_c1[11]),
    .C14(_16_Bit_parallel_adder_7_c1[13]), .C15(_16_Bit_parallel_adder_7_c1[14]),
    .C13(_16_Bit_parallel_adder_7_c1[12]));
  _16_Bit_parallel_adder _16_Bit_parallel_adder_8 (
    .A(_16_Bit_parallel_adder_7_c1), .B(_16_AND_Gates_8_c0), .Carry_Out(_16_Bit_parallel_adder_8_c1[15]),
    .C0(Result[8]), .C1(_16_Bit_parallel_adder_8_c1[0]), .C2(_16_Bit_parallel_adder_8_c1[1]),
    .C3(_16_Bit_parallel_adder_8_c1[2]), .C4(_16_Bit_parallel_adder_8_c1[3]),
    .C5(_16_Bit_parallel_adder_8_c1[4]), .C6(_16_Bit_parallel_adder_8_c1[5]),
    .C7(_16_Bit_parallel_adder_8_c1[6]), .C9(_16_Bit_parallel_adder_8_c1[7]),
    .C8(_16_Bit_parallel_adder_8_c1[8]), .C10(_16_Bit_parallel_adder_8_c1[9]),
    .C11(_16_Bit_parallel_adder_8_c1[10]), .C12(_16_Bit_parallel_adder_8_c1[11]),
    .C14(_16_Bit_parallel_adder_8_c1[13]), .C15(_16_Bit_parallel_adder_8_c1[14]),
    .C13(_16_Bit_parallel_adder_8_c1[12]));
  _16_Bit_parallel_adder _16_Bit_parallel_adder_9 (
    .A(_16_Bit_parallel_adder_8_c1), .B(_16_AND_Gates_9_c0), .Carry_Out(_16_Bit_parallel_adder_9_c1[15]),
    .C0(Result[9]), .C1(_16_Bit_parallel_adder_9_c1[0]), .C2(_16_Bit_parallel_adder_9_c1[1]),
    .C3(_16_Bit_parallel_adder_9_c1[2]), .C4(_16_Bit_parallel_adder_9_c1[3]),
    .C5(_16_Bit_parallel_adder_9_c1[4]), .C6(_16_Bit_parallel_adder_9_c1[5]),
    .C7(_16_Bit_parallel_adder_9_c1[6]), .C9(_16_Bit_parallel_adder_9_c1[7]),
    .C8(_16_Bit_parallel_adder_9_c1[8]), .C10(_16_Bit_parallel_adder_9_c1[9]),
    .C11(_16_Bit_parallel_adder_9_c1[10]), .C12(_16_Bit_parallel_adder_9_c1[11]),
    .C14(_16_Bit_parallel_adder_9_c1[13]), .C15(_16_Bit_parallel_adder_9_c1[14]),
    .C13(_16_Bit_parallel_adder_9_c1[12]));
  _16_Bit_parallel_adder _16_Bit_parallel_adder_10 (
    .A(_16_Bit_parallel_adder_9_c1), .B(_16_AND_Gates_10_c0), .Carry_Out(_16_Bit_parallel_adder_10_c1[15]),
    .C0(Result[10]), .C1(_16_Bit_parallel_adder_10_c1[0]), .C2(_16_Bit_parallel_adder_10_c1[1]),
    .C3(_16_Bit_parallel_adder_10_c1[2]), .C4(_16_Bit_parallel_adder_10_c1[3]),
    .C5(_16_Bit_parallel_adder_10_c1[4]), .C6(_16_Bit_parallel_adder_10_c1[5]),
    .C7(_16_Bit_parallel_adder_10_c1[6]), .C9(_16_Bit_parallel_adder_10_c1[7]),
    .C8(_16_Bit_parallel_adder_10_c1[8]), .C10(_16_Bit_parallel_adder_10_c1[9]),
    .C11(_16_Bit_parallel_adder_10_c1[10]), .C12(_16_Bit_parallel_adder_10_c1[11]),
    .C14(_16_Bit_parallel_adder_10_c1[13]), .C15(_16_Bit_parallel_adder_10_c1[14]),
    .C13(_16_Bit_parallel_adder_10_c1[12]));
  _16_Bit_parallel_adder _16_Bit_parallel_adder_11 (
    .A(_16_Bit_parallel_adder_10_c1), .B(_16_AND_Gates_11_c0), .Carry_Out(_16_Bit_parallel_adder_11_c1[15]),
    .C0(Result[11]), .C1(_16_Bit_parallel_adder_11_c1[0]), .C2(_16_Bit_parallel_adder_11_c1[1]),
    .C3(_16_Bit_parallel_adder_11_c1[2]), .C4(_16_Bit_parallel_adder_11_c1[3]),
    .C5(_16_Bit_parallel_adder_11_c1[4]), .C6(_16_Bit_parallel_adder_11_c1[5]),
    .C7(_16_Bit_parallel_adder_11_c1[6]), .C9(_16_Bit_parallel_adder_11_c1[7]),
    .C8(_16_Bit_parallel_adder_11_c1[8]), .C10(_16_Bit_parallel_adder_11_c1[9]),
    .C11(_16_Bit_parallel_adder_11_c1[10]), .C12(_16_Bit_parallel_adder_11_c1[11]),
    .C14(_16_Bit_parallel_adder_11_c1[13]), .C15(_16_Bit_parallel_adder_11_c1[14]),
    .C13(_16_Bit_parallel_adder_11_c1[12]));
  _16_Bit_parallel_adder _16_Bit_parallel_adder_12 (
    .A(_16_Bit_parallel_adder_11_c1), .B(_16_AND_Gates_12_c0), .Carry_Out(_16_Bit_parallel_adder_12_c1[15]),
    .C0(Result[12]), .C1(_16_Bit_parallel_adder_12_c1[0]), .C2(_16_Bit_parallel_adder_12_c1[1]),
    .C3(_16_Bit_parallel_adder_12_c1[2]), .C4(_16_Bit_parallel_adder_12_c1[3]),
    .C5(_16_Bit_parallel_adder_12_c1[4]), .C6(_16_Bit_parallel_adder_12_c1[5]),
    .C7(_16_Bit_parallel_adder_12_c1[6]), .C9(_16_Bit_parallel_adder_12_c1[7]),
    .C8(_16_Bit_parallel_adder_12_c1[8]), .C10(_16_Bit_parallel_adder_12_c1[9]),
    .C11(_16_Bit_parallel_adder_12_c1[10]), .C12(_16_Bit_parallel_adder_12_c1[11]),
    .C14(_16_Bit_parallel_adder_12_c1[13]), .C15(_16_Bit_parallel_adder_12_c1[14]),
    .C13(_16_Bit_parallel_adder_12_c1[12]));
  _16_Bit_parallel_adder _16_Bit_parallel_adder_13 (
    .A(_16_Bit_parallel_adder_12_c1), .B(_16_AND_Gates_14_c0), .Carry_Out(_16_Bit_parallel_adder_13_c1[15]),
    .C0(Result[13]), .C1(_16_Bit_parallel_adder_13_c1[0]), .C2(_16_Bit_parallel_adder_13_c1[1]),
    .C3(_16_Bit_parallel_adder_13_c1[2]), .C4(_16_Bit_parallel_adder_13_c1[3]),
    .C5(_16_Bit_parallel_adder_13_c1[4]), .C6(_16_Bit_parallel_adder_13_c1[5]),
    .C7(_16_Bit_parallel_adder_13_c1[6]), .C9(_16_Bit_parallel_adder_13_c1[7]),
    .C8(_16_Bit_parallel_adder_13_c1[8]), .C10(_16_Bit_parallel_adder_13_c1[9]),
    .C11(_16_Bit_parallel_adder_13_c1[10]), .C12(_16_Bit_parallel_adder_13_c1[11]),
    .C14(_16_Bit_parallel_adder_13_c1[13]), .C15(_16_Bit_parallel_adder_13_c1[14]),
    .C13(_16_Bit_parallel_adder_13_c1[12]));
  _16_Bit_parallel_adder _16_Bit_parallel_adder_14 (
    .A(_16_Bit_parallel_adder_13_c1), .B(_16_AND_Gates_15_c0), .Carry_Out(_16_Bit_parallel_adder_14_c1[15]),
    .C0(Result[14]), .C1(_16_Bit_parallel_adder_14_c1[0]), .C2(_16_Bit_parallel_adder_14_c1[1]),
    .C3(_16_Bit_parallel_adder_14_c1[2]), .C4(_16_Bit_parallel_adder_14_c1[3]),
    .C5(_16_Bit_parallel_adder_14_c1[4]), .C6(_16_Bit_parallel_adder_14_c1[5]),
    .C7(_16_Bit_parallel_adder_14_c1[6]), .C9(_16_Bit_parallel_adder_14_c1[7]),
    .C8(_16_Bit_parallel_adder_14_c1[8]), .C10(_16_Bit_parallel_adder_14_c1[9]),
    .C11(_16_Bit_parallel_adder_14_c1[10]), .C12(_16_Bit_parallel_adder_14_c1[11]),
    .C14(_16_Bit_parallel_adder_14_c1[13]), .C15(_16_Bit_parallel_adder_14_c1[14]),
    .C13(_16_Bit_parallel_adder_14_c1[12]));
  _16_Bit_parallel_adder _16_Bit_parallel_adder_15 (
    .A(_16_Bit_parallel_adder_14_c1), .B(_16_AND_Gates_16_c0), .Carry_Out(Result[31]), .C0(Result[15]),
    .C1(Result[16]), .C2(Result[17]), .C3(Result[18]), .C4(Result[19]), .C5(Result[20]), .C6(Result[21]),
    .C7(Result[22]), .C9(Result[23]), .C8(Result[24]), .C10(Result[25]), .C11(Result[26]), .C12(Result[27]),
    .C14(Result[29]), .C15(Result[30]), .C13(Result[28]));
endmodule

module _4_bit_parallel_adder (
  input  Carry_In,
  input  A,
  input  B,
  input  C,
  input  D,
  input  E,
  input  F,
  input  G,
  input  H,
  output C1,
  output C2,
  output C3,
  output C4,
  output Carry_Out
);

  wire adder_1_cout, adder_2_cout, adder_3_cout;

  Adder #(.width(1)) adder_1 (.a(A), .b(B), .out(C1), .cin(Carry_In), .cout(adder_1_cout));
  Adder #(.width(1)) adder_2 (.a(C), .b(D), .out(C2), .cin(adder_1_cout), .cout(adder_2_cout));
  Adder #(.width(1)) adder_3 (.a(E), .b(F), .out(C3), .cin(adder_2_cout), .cout(adder_3_cout));
  Adder #(.width(1)) adder_4 (.a(G), .b(H), .out(C4), .cin(adder_3_cout), .cout(Carry_Out));
endmodule

module _16_Bit_parallel_adder (
  input  [15:0] A,
  input  [15:0] B,
  output C0,
  output C1,
  output C2,
  output C3,
  output C4,
  output C5,
  output C6,
  output C7,
  output C8,
  output C9,
  output C10,
  output C11,
  output C12,
  output C13,
  output C14,
  output C15,
  output Carry_Out
);

  wire n4_bit_parallel_adder_1_carry_out, n4_bit_parallel_adder_2_carry_out,
       n4_bit_parallel_adder_3_carry_out;

  _4_bit_parallel_adder u_4_bit_parallel_adder_1 (
    .A(A[0]), .B(B[0]), .C(A[1]), .D(B[1]), .E(A[2]), .F(B[2]), .G(A[3]), .H(B[3]),
    .Carry_Out(n4_bit_parallel_adder_1_carry_out), .C1(C0), .C2(C1), .C3(C2), .C4(C3));  // open: Carry_In
  _4_bit_parallel_adder u_4_bit_parallel_adder_2 (
    .A(A[4]), .B(B[4]), .C(A[5]), .D(B[5]), .E(A[6]), .F(B[6]), .G(A[7]), .H(B[7]),
    .Carry_Out(n4_bit_parallel_adder_2_carry_out), .C1(C4), .C2(C5), .C3(C6), .C4(C7),
    .Carry_In(n4_bit_parallel_adder_1_carry_out));
  _4_bit_parallel_adder u_4_bit_parallel_adder_3 (
    .A(A[8]), .B(B[8]), .C(A[9]), .D(B[9]), .E(A[10]), .F(B[10]), .G(A[11]), .H(B[11]),
    .Carry_Out(n4_bit_parallel_adder_3_carry_out), .C1(C8), .C2(C9), .C3(C10), .C4(C11),
    .Carry_In(n4_bit_parallel_adder_2_carry_out));
  _4_bit_parallel_adder u_4_bit_parallel_adder_4 (
    .A(A[12]), .B(B[12]), .C(A[13]), .D(B[13]), .E(A[14]), .F(B[14]), .G(A[15]), .H(B[15]),
    .Carry_Out(Carry_Out), .C1(C12), .C2(C13), .C3(C14), .C4(C15),
    .Carry_In(n4_bit_parallel_adder_3_carry_out));
endmodule

module _16_And_Gates (
  input  [15:0] B,
  input  in_2,
  output C15,
  output C14,
  output C13,
  output C12,
  output C11,
  output C10,
  output C9,
  output C8,
  output C7,
  output C6,
  output C5,
  output C4,
  output C3,
  output C2,
  output C1,
  output C0
);

  and and_1 (C15, in_2, B[15]);
  and and_2 (C13, in_2, B[13]);
  and and_3 (C14, in_2, B[14]);
  and and_4 (C12, in_2, B[12]);
  and and_5 (C11, in_2, B[11]);
  and and_6 (C10, in_2, B[10]);
  and and_7 (C9, in_2, B[9]);
  and and_8 (C8, in_2, B[8]);
  and and_9 (C7, in_2, B[7]);
  and and_10 (C5, in_2, B[5]);
  and and_11 (C6, in_2, B[6]);
  and and_12 (C3, in_2, B[3]);
  and and_13 (C4, in_2, B[4]);
  and and_14 (C2, in_2, B[2]);
  and and_15 (C1, in_2, B[1]);
  and and_16 (C0, in_2, B[0]);
endmodule
